# Fritzing sketch gsclock_arduino_uno_sketch (saved by Fritzing 0.9.6b)
breadboards: 1

parts:
  パーツ1 = Arduino Uno (Rev3) - ICSP
  Part1 = KY-015 Temperature & Humidity Sensor Module [package="Breakout board"]
  LED1 = LED - 5mm [color="Red (633nm)" current=0.030 package="5 mm [THT]"]
  S1 = Pushbutton [package="[THT]"]
  R1 = Resistor [tolerance=±5% power=0.25 resistance=1k package=THT]
  R3 = Photocell (LDR) [package=THT]
  R4 = Resistor [tolerance=±5% power=0.25 resistance=1k package=THT]
  Pulldown_Regsiter = Resistor [tolerance=±5% power=0.25 resistance=10k package=THT]

nets:
  N1: パーツ1.A0, R3.pin_1, R4.Pin_0
  N2: パーツ1.GND, Part1.-, LED1.cathode, R4.Pin_1, Pulldown_Regsiter.Pin_1
  N3: パーツ1.D2, S1.Pin_1, S1.Pin_2, Pulldown_Regsiter.Pin_0
  N4: パーツ1.D4, Part1.Vin, R1.Pin_1, R3.pin_0
  N5: パーツ1.D7, Part1.S
  N6: パーツ1.5V, S1.Pin_3, S1.Pin_4
  N7: LED1.anode, R1.Pin_0

custom parts:
  KY-015 Temperature & Humidity Sensor Module: DH-11 temperature and humidity sensor in KEYES KY-015 module, provides a low-latency serial interface to measure humidity and temperature.
